# Fritzing sketch circuit (saved by Fritzing 0.9.3b)
circuit board: 8.46667cm x 5.64444cm
breadboards: 1

parts:
  R1 = Resistor [tolerance=±5% resistance=1k package=THT]
  R2 = Resistor [tolerance=±5% resistance=1k package=THT]
  Q1 = TRANSISTOR_NPN [part_number=2N3904 package=to-92]
  Q2 = TRANSISTOR_NPN [part_number=2N3904 package=to-92]

nets:
  D1: R1.Pin_0
  N1: R1.Pin_1, Q1.B
  D2: R2.Pin_0
  N2: R2.Pin_1, Q2.B
  GND: Q1.E, Q2.E
  LED1 GND: Q1.C
  LED2 GND: Q2.C
